// Logisim project 150119037_150119036_150119566.circ as structural Verilog: 17 circuits, main circuit main
module main (
);

  wire alu_1_equalflag, and_1_out, and_2_out, clock_1_out, controlunit_1_branch, controlunit_1_jump,
       controlunit_1_memread, controlunit_1_memwrite, controlunit_1_pcwrite, controlunit_1_regwrite,
       controlunit_1_regwriteselect, controlunit_1_stackwrite, not_1_out, not_2_out, or_1_out;
  wire [3:0] rom_1_data_2;
  wire [9:0] multiplexer_1_out, multiplexer_2_out, multiplexer_3_out, multiplexer_4_out, multiplexer_5_out,
       n10bitadder_1_out_3, n10bitadder_2_out_3, n10bitadder_3_out_3, n10bitadder_4_out_3,
       Program_Counter_output, Stack_Pointer_output;
  wire [15:0] rom_1_data;
  wire [19:0] alu_1_result, multiplexer_6_out, multiplexer_7_out, multiplexer_8_out, n7_20signextend_1_out_2,
       n20bitregister_1_out_4, ram_1_data, registerfile_1_destoutput, registerfile_1_readoutput,
       registerfile_1_readoutput2;

  _10BitRegister Program_Counter (
    .Clock(clock_1_out), .Data(multiplexer_1_out), .Enable(controlunit_1_pcwrite),
    .Output(Program_Counter_output));
  _10BitAdder u_10bitadder_1 (.A(Program_Counter_output), .B(10'h1), .out_3(n10bitadder_1_out_3));
  ROM #(.addrWidth(10), .dataWidth(20)) rom_1 (
    .addr(Program_Counter_output), .data({rom_1_data_2, rom_1_data}));  // open: sel
  _10BitAdder u_10bitadder_2 (.A(Stack_Pointer_output), .B(10'h1), .out_3(n10bitadder_2_out_3));
  Multiplexer #(.width(10)) multiplexer_1 (
    .in0(multiplexer_4_out), .in1(n10bitadder_3_out_3), .out(multiplexer_1_out), .sel(controlunit_1_jump));  // open: en
  Multiplexer #(.width(10)) multiplexer_2 (
    .in0(n10bitadder_4_out_3), .in1(n10bitadder_2_out_3), .out(multiplexer_2_out), .sel(rom_1_data_2[0]));  // open: en
  _10BitAdder u_10bitadder_3 (.A(Program_Counter_output), .B(rom_1_data[15:6]), .out_3(n10bitadder_3_out_3));
  _10BitRegister Stack_Pointer (
    .Clock(clock_1_out), .Data(multiplexer_2_out), .Enable(controlunit_1_stackwrite),
    .Output(Stack_Pointer_output));
  Multiplexer #(.width(10)) multiplexer_3 (
    .in0(n10bitadder_4_out_3), .in1(Stack_Pointer_output), .out(multiplexer_3_out), .sel(rom_1_data_2[0]));  // open: en
  _10BitAdder u_10bitadder_4 (.A(Stack_Pointer_output), .B({10{1'b1}}), .out_3(n10bitadder_4_out_3));
  Multiplexer #(.width(10)) multiplexer_4 (
    .in0(n10bitadder_1_out_3), .in1({Program_Counter_output[9:7], rom_1_data[6:0]}), .out(multiplexer_4_out),
    .sel(or_1_out));  // open: en
  and and_1 (and_1_out, controlunit_1_branch, not_1_out, alu_1_equalflag);
  or or_1 (or_1_out, and_1_out, and_2_out);
  and and_2 (and_2_out, controlunit_1_branch, rom_1_data_2[0], not_2_out);
  _7_20SignExtend u_7_20signextend_1 (.in_1(rom_1_data[6:0]), .out_2(n7_20signextend_1_out_2));
  Multiplexer #(.width(10)) multiplexer_5 (
    .in0(rom_1_data[9:0]), .in1(multiplexer_3_out), .out(multiplexer_5_out), .sel(rom_1_data[15]));  // open: en
  Clock clock_1 (.out(clock_1_out));
  not not_1 (not_1_out, rom_1_data_2[0]);
  not not_2 (not_2_out, alu_1_equalflag);
  RegisterFile registerfile_1 (
    .WriteAddress(rom_1_data[14:11]), .Clock(clock_1_out), .readOutput(registerfile_1_readoutput),
    .WriteEnable(controlunit_1_regwrite), .WriteData(multiplexer_8_out), .ReadAddress(rom_1_data[10:7]),
    .ReadAddress2(rom_1_data[6:3]), .readOutput2(registerfile_1_readoutput2),
    .DestOutput(registerfile_1_destoutput));
  Multiplexer #(.width(20)) multiplexer_6 (
    .in0(registerfile_1_readoutput2), .in1(n7_20signextend_1_out_2), .out(multiplexer_6_out),
    .sel(rom_1_data[15]));  // open: en
  ALU alu_1 (
    .in1(registerfile_1_readoutput), .in2(multiplexer_7_out), .opCode(rom_1_data_2[2:0]),
    .result(alu_1_result), .EqualFlag(alu_1_equalflag));
  Multiplexer #(.width(20)) multiplexer_7 (
    .in0(multiplexer_6_out), .in1(registerfile_1_destoutput), .out(multiplexer_7_out),
    .sel(controlunit_1_branch));  // open: en
  Multiplexer #(.width(20)) multiplexer_8 (
    .in0(alu_1_result), .in1(n20bitregister_1_out_4), .out(multiplexer_8_out),
    .sel(controlunit_1_regwriteselect));  // open: en
  RAM #(.addrWidth(10), .dataWidth(20), .bus("separate")) ram_1 (
    .addr(multiplexer_5_out), .din(registerfile_1_destoutput), .data(ram_1_data),
    .str(controlunit_1_memwrite), .clk(clock_1_out), .ld(controlunit_1_memread));  // open: sel, clr
  _20BitRegister u_20bitregister_1 (
    .Clock(clock_1_out), .in_2(ram_1_data), .out_4(n20bitregister_1_out_4), .Enable(controlunit_1_memread));
  ControlUnit controlunit_1 (
    .Clock(clock_1_out), .Opcode(rom_1_data_2), .RegWrite(controlunit_1_regwrite),
    .PCWrite(controlunit_1_pcwrite), .MemWrite(controlunit_1_memwrite), .MemRead(controlunit_1_memread),
    .Jump(controlunit_1_jump), .Branch(controlunit_1_branch), .StackWrite(controlunit_1_stackwrite),
    .RegWriteSelect(controlunit_1_regwriteselect));

  // Notes on the sheet:
  //   Instruction Memory
  //   contents of rom_1 (hex, n*v repeats v):
  //   50000 50801 41110 29980 1980 9101 b0904 89800 51802 9a000 19a0 19981 61803 7ffc0
  //   Data Memory
endmodule

module ALU (
  input  [19:0] in1,
  input  [19:0] in2,
  input  [2:0] opCode,
  output EqualFlag,
  output [19:0] result
);

  wire and_2_out, and_3_out, and_4_out;
  wire [1:0] or_3_out;
  wire [19:0] and_1_out, multiplexer_1_out, n20_bit_adder_1_out_4, not_1_out, or_1_out, xor_1_out;

  assign not_1_out = ~in2;  // NOT_Gate not_1, 20 bits wide
  Multiplexer #(.width(20)) multiplexer_1 (
    .in0(in2), .in1(not_1_out), .out(multiplexer_1_out), .sel(opCode[0]));  // open: en
  _20BitComparator u_20bitcomparator_1 (.A(in1), .B(in2), .Eq(EqualFlag));  // open: Lt, Gt
  _20_bit_adder u_20_bit_adder_1 (
    .Cin(opCode[0]), .A(in1), .B(multiplexer_1_out), .out_4(n20_bit_adder_1_out_4));  // open: Cout
  assign and_1_out = in1 & in2;  // AND_Gate and_1, 20 bits wide
  assign or_1_out = in1 | in2;  // OR_Gate or_1, 20 bits wide
  assign xor_1_out = in1 ^ in2;  // XOR_Gate xor_1, 20 bits wide
  and and_2 (and_2_out, opCode[0], opCode[1], ~opCode[2]);  // AND_Gate
  and and_3 (and_3_out, opCode[2], ~opCode[0], ~opCode[1]);  // AND_Gate
  and and_4 (and_4_out, ~opCode[2], opCode[1], ~opCode[0]);  // AND_Gate
  or or_2 (or_3_out[1], and_2_out, and_3_out);
  or or_3 (or_3_out[0], and_3_out, and_4_out);
  Multiplexer #(.select(2), .width(20)) multiplexer_2 (
    .in0(n20_bit_adder_1_out_4), .in1(and_1_out), .in2(or_1_out), .in3(xor_1_out), .out(result),
    .sel(or_3_out));  // open: en
endmodule

module RegisterFile (
  input  WriteEnable,
  input  [19:0] WriteData,
  input  [3:0] WriteAddress,
  input  Clock,
  input  [3:0] ReadAddress,
  input  [3:0] ReadAddress2,
  output [19:0] readOutput,
  output [19:0] readOutput2,
  output [19:0] DestOutput
);

  wire and_1_out, and_2_out, and_3_out, and_4_out, and_5_out, and_6_out, and_7_out, and_8_out, and_9_out,
       and_10_out, and_11_out, and_12_out, and_13_out, and_14_out, and_15_out, and_16_out, decoder_1_out0,
       decoder_1_out1, decoder_1_out2, decoder_1_out3, decoder_2_out0, decoder_2_out1, decoder_2_out2,
       decoder_2_out3;
  wire [19:0] n20bitregister_1_out_4, n20bitregister_2_out_4, n20bitregister_3_out_4, n20bitregister_4_out_4,
       n20bitregister_5_out_4, n20bitregister_6_out_4, n20bitregister_7_out_4, n20bitregister_8_out_4,
       n20bitregister_9_out_4, n20bitregister_10_out_4, n20bitregister_11_out_4, n20bitregister_12_out_4,
       n20bitregister_13_out_4, n20bitregister_14_out_4, n20bitregister_15_out_4, n20bitregister_16_out_4;

  Decoder #(.select(2)) decoder_1 (
    .out0(decoder_1_out0), .out1(decoder_1_out1), .out2(decoder_1_out2), .out3(decoder_1_out3),
    .sel(WriteAddress[1:0]));  // open: en
  Decoder #(.select(2)) decoder_2 (
    .out0(decoder_2_out0), .out1(decoder_2_out1), .out2(decoder_2_out2), .out3(decoder_2_out3),
    .sel(WriteAddress[3:2]));  // open: en
  _20BitRegister u_20bitregister_1 (
    .Clock(Clock), .in_2(WriteData), .out_4(n20bitregister_1_out_4), .Enable(and_1_out));
  and and_1 (and_1_out, WriteEnable, decoder_1_out0, decoder_2_out0);
  _20BitRegister u_20bitregister_2 (
    .Clock(Clock), .in_2(WriteData), .out_4(n20bitregister_2_out_4), .Enable(and_2_out));
  and and_2 (and_2_out, WriteEnable, decoder_1_out0, decoder_2_out1);
  _20BitRegister u_20bitregister_3 (
    .Clock(Clock), .in_2(WriteData), .out_4(n20bitregister_3_out_4), .Enable(and_3_out));
  and and_3 (and_3_out, WriteEnable, decoder_1_out0, decoder_2_out2);
  _20BitRegister u_20bitregister_4 (
    .Clock(Clock), .in_2(WriteData), .out_4(n20bitregister_4_out_4), .Enable(and_4_out));
  and and_4 (and_4_out, WriteEnable, decoder_1_out0, decoder_2_out3);
  and and_5 (and_5_out, WriteEnable, decoder_1_out1, decoder_2_out0);
  and and_6 (and_6_out, WriteEnable, decoder_1_out1, decoder_2_out1);
  and and_7 (and_7_out, WriteEnable, decoder_1_out1, decoder_2_out2);
  and and_8 (and_8_out, WriteEnable, decoder_1_out1, decoder_2_out3);
  _20BitRegister u_20bitregister_5 (
    .Clock(Clock), .in_2(WriteData), .out_4(n20bitregister_5_out_4), .Enable(and_5_out));
  _20BitRegister u_20bitregister_6 (
    .Clock(Clock), .in_2(WriteData), .out_4(n20bitregister_6_out_4), .Enable(and_6_out));
  _20BitRegister u_20bitregister_7 (
    .Clock(Clock), .in_2(WriteData), .out_4(n20bitregister_7_out_4), .Enable(and_7_out));
  _20BitRegister u_20bitregister_8 (
    .Clock(Clock), .in_2(WriteData), .out_4(n20bitregister_8_out_4), .Enable(and_8_out));
  _20BitRegister u_20bitregister_9 (
    .Clock(Clock), .in_2(WriteData), .out_4(n20bitregister_9_out_4), .Enable(and_9_out));
  and and_9 (and_9_out, WriteEnable, decoder_1_out2, decoder_2_out0);
  _20BitRegister u_20bitregister_10 (
    .Clock(Clock), .in_2(WriteData), .out_4(n20bitregister_10_out_4), .Enable(and_10_out));
  and and_10 (and_10_out, WriteEnable, decoder_1_out2, decoder_2_out1);
  _20BitRegister u_20bitregister_11 (
    .Clock(Clock), .in_2(WriteData), .out_4(n20bitregister_11_out_4), .Enable(and_11_out));
  and and_11 (and_11_out, WriteEnable, decoder_1_out2, decoder_2_out2);
  _20BitRegister u_20bitregister_12 (
    .Clock(Clock), .in_2(WriteData), .out_4(n20bitregister_12_out_4), .Enable(and_12_out));
  and and_12 (and_12_out, WriteEnable, decoder_1_out2, decoder_2_out3);
  and and_13 (and_13_out, WriteEnable, decoder_1_out3, decoder_2_out0);
  and and_14 (and_14_out, WriteEnable, decoder_1_out3, decoder_2_out1);
  and and_15 (and_15_out, WriteEnable, decoder_1_out3, decoder_2_out2);
  and and_16 (and_16_out, WriteEnable, decoder_1_out3, decoder_2_out3);
  _20BitRegister u_20bitregister_13 (
    .Clock(Clock), .in_2(WriteData), .out_4(n20bitregister_13_out_4), .Enable(and_13_out));
  _20BitRegister u_20bitregister_14 (
    .Clock(Clock), .in_2(WriteData), .out_4(n20bitregister_14_out_4), .Enable(and_14_out));
  _20BitRegister u_20bitregister_15 (
    .Clock(Clock), .in_2(WriteData), .out_4(n20bitregister_15_out_4), .Enable(and_15_out));
  _20BitRegister u_20bitregister_16 (
    .Clock(Clock), .in_2(WriteData), .out_4(n20bitregister_16_out_4), .Enable(and_16_out));
  Multiplexer #(.select(4), .width(20)) multiplexer_1 (
    .in0(n20bitregister_1_out_4), .in1(n20bitregister_5_out_4), .in2(n20bitregister_9_out_4),
    .in3(n20bitregister_13_out_4), .in4(n20bitregister_2_out_4), .in5(n20bitregister_6_out_4),
    .in6(n20bitregister_10_out_4), .in7(n20bitregister_14_out_4), .in8(n20bitregister_3_out_4),
    .in9(n20bitregister_7_out_4), .in10(n20bitregister_11_out_4), .in11(n20bitregister_15_out_4),
    .in12(n20bitregister_4_out_4), .in13(n20bitregister_8_out_4), .in14(n20bitregister_12_out_4),
    .in15(n20bitregister_16_out_4), .out(readOutput), .sel(ReadAddress));  // open: en
  Multiplexer #(.select(4), .width(20)) multiplexer_2 (
    .in0(n20bitregister_1_out_4), .in1(n20bitregister_5_out_4), .in2(n20bitregister_9_out_4),
    .in3(n20bitregister_13_out_4), .in4(n20bitregister_2_out_4), .in5(n20bitregister_6_out_4),
    .in6(n20bitregister_10_out_4), .in7(n20bitregister_14_out_4), .in8(n20bitregister_3_out_4),
    .in9(n20bitregister_7_out_4), .in10(n20bitregister_11_out_4), .in11(n20bitregister_15_out_4),
    .in12(n20bitregister_4_out_4), .in13(n20bitregister_8_out_4), .in14(n20bitregister_12_out_4),
    .in15(n20bitregister_16_out_4), .out(readOutput2), .sel(ReadAddress2));  // open: en
  Multiplexer #(.select(4), .width(20)) multiplexer_3 (
    .in0(n20bitregister_1_out_4), .in1(n20bitregister_5_out_4), .in2(n20bitregister_9_out_4),
    .in3(n20bitregister_13_out_4), .in4(n20bitregister_2_out_4), .in5(n20bitregister_6_out_4),
    .in6(n20bitregister_10_out_4), .in7(n20bitregister_14_out_4), .in8(n20bitregister_3_out_4),
    .in9(n20bitregister_7_out_4), .in10(n20bitregister_11_out_4), .in11(n20bitregister_15_out_4),
    .in12(n20bitregister_4_out_4), .in13(n20bitregister_8_out_4), .in14(n20bitregister_12_out_4),
    .in15(n20bitregister_16_out_4), .out(DestOutput), .sel(WriteAddress));  // open: en
endmodule

module FullAdder (
  input  Cin,
  input  A,
  input  B,
  output Sum,
  output Cout
);

  wire and_1_out, and_2_out, xor_1_out;

  xor xor_1 (xor_1_out, A, B);
  xor xor_2 (Sum, xor_1_out, Cin);
  and and_1 (and_1_out, Cin, xor_1_out);
  and and_2 (and_2_out, B, A);
  or or_1 (Cout, and_1_out, and_2_out);
endmodule

module _4_bit_adder (
  input  Cin,
  input  [3:0] in_2,
  input  [3:0] in_3,
  output [3:0] Sum,
  output Cout
);

  wire fulladder_1_cout, fulladder_2_cout, fulladder_3_cout;

  FullAdder fulladder_1 (.Cin(Cin), .A(in_2[0]), .B(in_3[0]), .Sum(Sum[0]), .Cout(fulladder_1_cout));
  FullAdder fulladder_2 (.Cin(fulladder_1_cout), .A(in_2[1]), .B(in_3[1]), .Sum(Sum[1]), .Cout(fulladder_2_cout));
  FullAdder fulladder_3 (.Cin(fulladder_2_cout), .A(in_2[2]), .B(in_3[2]), .Sum(Sum[2]), .Cout(fulladder_3_cout));
  FullAdder fulladder_4 (.Cin(fulladder_3_cout), .A(in_2[3]), .B(in_3[3]), .Sum(Sum[3]), .Cout(Cout));
endmodule

// +
module _20_bit_adder (
  input  Cin,
  input  [19:0] A,
  input  [19:0] B,
  output [19:0] out_4,
  output Cout
);

  wire n4_bit_adder_1_cout, n4_bit_adder_2_cout, n4_bit_adder_3_cout, n4_bit_adder_4_cout;

  _4_bit_adder u_4_bit_adder_1 (.Cin(Cin), .in_2(A[3:0]), .in_3(B[3:0]), .Sum(out_4[3:0]), .Cout(n4_bit_adder_1_cout));
  _4_bit_adder u_4_bit_adder_2 (
    .Cin(n4_bit_adder_1_cout), .in_2(A[7:4]), .in_3(B[7:4]), .Sum(out_4[7:4]), .Cout(n4_bit_adder_2_cout));
  _4_bit_adder u_4_bit_adder_3 (
    .Cin(n4_bit_adder_2_cout), .in_2(A[11:8]), .in_3(B[11:8]), .Sum(out_4[11:8]), .Cout(n4_bit_adder_3_cout));
  _4_bit_adder u_4_bit_adder_4 (
    .Cin(n4_bit_adder_3_cout), .in_2(A[15:12]), .in_3(B[15:12]), .Sum(out_4[15:12]),
    .Cout(n4_bit_adder_4_cout));
  _4_bit_adder u_4_bit_adder_5 (
    .Cin(n4_bit_adder_4_cout), .in_2(A[19:16]), .in_3(B[19:16]), .Sum(out_4[19:16]), .Cout(Cout));
endmodule

module FullComparator (
  input  LtIn,
  input  GtIn,
  input  EqIn,
  input  A,
  input  B,
  output Lt,
  output Gt,
  output Eq
);

  wire and_1_out, and_2_out, and_3_out, and_4_out, not_1_out, not_2_out, not_3_out, not_4_out;

  not not_1 (not_1_out, A);
  not not_2 (not_2_out, B);
  not not_3 (not_3_out, A);
  not not_4 (not_4_out, B);
  or or_1 (Lt, LtIn, and_1_out);
  and and_1 (and_1_out, EqIn, not_1_out, B);
  or or_2 (Gt, GtIn, and_2_out);
  and and_2 (and_2_out, EqIn, A, not_2_out);
  and and_3 (and_3_out, EqIn, A, B);
  or or_3 (Eq, and_3_out, and_4_out);
  and and_4 (and_4_out, EqIn, not_3_out, not_4_out);
endmodule

module _4BitComparator (
  input  LtIn,
  input  GtIn,
  input  EqIn,
  input  [3:0] in_4,
  input  [3:0] in_5,
  output Lt,
  output Gt,
  output Eq
);

  wire fullcomparator_1_eq, fullcomparator_1_gt, fullcomparator_1_lt, fullcomparator_2_eq,
       fullcomparator_2_gt, fullcomparator_2_lt, fullcomparator_3_eq, fullcomparator_3_gt,
       fullcomparator_3_lt;

  FullComparator fullcomparator_1 (
    .LtIn(LtIn), .GtIn(GtIn), .EqIn(EqIn), .A(in_4[3]), .B(in_5[3]), .Lt(fullcomparator_1_lt),
    .Gt(fullcomparator_1_gt), .Eq(fullcomparator_1_eq));
  FullComparator fullcomparator_2 (
    .LtIn(fullcomparator_1_lt), .GtIn(fullcomparator_1_gt), .EqIn(fullcomparator_1_eq), .A(in_4[2]),
    .B(in_5[2]), .Lt(fullcomparator_2_lt), .Gt(fullcomparator_2_gt), .Eq(fullcomparator_2_eq));
  FullComparator fullcomparator_3 (
    .LtIn(fullcomparator_2_lt), .GtIn(fullcomparator_2_gt), .EqIn(fullcomparator_2_eq), .A(in_4[1]),
    .B(in_5[1]), .Lt(fullcomparator_3_lt), .Gt(fullcomparator_3_gt), .Eq(fullcomparator_3_eq));
  FullComparator fullcomparator_4 (
    .LtIn(fullcomparator_3_lt), .GtIn(fullcomparator_3_gt), .EqIn(fullcomparator_3_eq), .A(in_4[0]),
    .B(in_5[0]), .Lt(Lt), .Gt(Gt), .Eq(Eq));
endmodule

module _20BitComparator (
  input  [19:0] A,
  input  [19:0] B,
  output Lt,
  output Gt,
  output Eq
);

  wire n4bitcomparator_1_eq, n4bitcomparator_1_gt, n4bitcomparator_1_lt, n4bitcomparator_2_eq,
       n4bitcomparator_2_gt, n4bitcomparator_2_lt, n4bitcomparator_3_eq, n4bitcomparator_3_gt,
       n4bitcomparator_3_lt, n4bitcomparator_4_eq, n4bitcomparator_4_gt, n4bitcomparator_4_lt;

  _4BitComparator u_4bitcomparator_1 (
    .LtIn(1'b0), .GtIn(1'b0), .EqIn(1'b1), .in_4(A[19:16]), .in_5(B[19:16]), .Lt(n4bitcomparator_1_lt),
    .Gt(n4bitcomparator_1_gt), .Eq(n4bitcomparator_1_eq));
  _4BitComparator u_4bitcomparator_2 (
    .LtIn(n4bitcomparator_1_lt), .GtIn(n4bitcomparator_1_gt), .EqIn(n4bitcomparator_1_eq), .in_4(A[15:12]),
    .in_5(B[15:12]), .Lt(n4bitcomparator_2_lt), .Gt(n4bitcomparator_2_gt), .Eq(n4bitcomparator_2_eq));
  _4BitComparator u_4bitcomparator_3 (
    .LtIn(n4bitcomparator_2_lt), .GtIn(n4bitcomparator_2_gt), .EqIn(n4bitcomparator_2_eq), .in_4(A[11:8]),
    .in_5(B[11:8]), .Lt(n4bitcomparator_3_lt), .Gt(n4bitcomparator_3_gt), .Eq(n4bitcomparator_3_eq));
  _4BitComparator u_4bitcomparator_4 (
    .LtIn(n4bitcomparator_3_lt), .GtIn(n4bitcomparator_3_gt), .EqIn(n4bitcomparator_3_eq), .in_4(A[7:4]),
    .in_5(B[7:4]), .Lt(n4bitcomparator_4_lt), .Gt(n4bitcomparator_4_gt), .Eq(n4bitcomparator_4_eq));
  _4BitComparator u_4bitcomparator_5 (
    .LtIn(n4bitcomparator_4_lt), .GtIn(n4bitcomparator_4_gt), .EqIn(n4bitcomparator_4_eq), .in_4(A[3:0]),
    .in_5(B[3:0]), .Lt(Lt), .Gt(Gt), .Eq(Eq));
endmodule

// SignExtend
module _7_20SignExtend (
  input  [6:0] in_1,
  output [19:0] out_2
);

  Multiplexer multiplexer_1 (.in0(1'b0), .in1(1'b1), .out(out_2[19]), .sel(in_1[6]));  // open: en

  assign out_2[18:0] = {{12{out_2[19]}}, in_1};
endmodule

// +
module _10BitAdder (
  input  [9:0] A,
  input  [9:0] B,
  output [9:0] out_3
);

  wire n4_bit_adder_1_cout, n4_bit_adder_2_cout;
  wire [3:0] bit_extender_1_out, bit_extender_2_out;
  wire [3:2] n4_bit_adder_3_sum;

  assign bit_extender_1_out = {{2{1'b0}}, B[9:8]};  // Bit_Extender bit_extender_1
  assign bit_extender_2_out = {{2{1'b0}}, A[9:8]};  // Bit_Extender bit_extender_2
  _4_bit_adder u_4_bit_adder_1 (.Cin(1'b0), .in_2(A[3:0]), .in_3(B[3:0]), .Sum(out_3[3:0]), .Cout(n4_bit_adder_1_cout));
  _4_bit_adder u_4_bit_adder_2 (
    .Cin(n4_bit_adder_1_cout), .in_2(A[7:4]), .in_3(B[7:4]), .Sum(out_3[7:4]), .Cout(n4_bit_adder_2_cout));
  _4_bit_adder u_4_bit_adder_3 (
    .Cin(n4_bit_adder_2_cout), .in_2(bit_extender_2_out), .in_3(bit_extender_1_out),
    .Sum({n4_bit_adder_3_sum, out_3[9:8]}));  // open: Cout
endmodule

// Reg
module _4BitRegister (
  input  Clock,
  input  [3:0] Data,
  input  Enable,
  output [3:0] Output
);

  D_Flip_Flop d_ff_1 (.clk(Clock), .D(Data[0]), .Q(Output[0]), .en(Enable));  // open: Qn, preset, reset
  D_Flip_Flop d_ff_2 (.clk(Clock), .D(Data[1]), .Q(Output[1]), .en(Enable));  // open: Qn, preset, reset
  D_Flip_Flop d_ff_3 (.clk(Clock), .D(Data[2]), .Q(Output[2]), .en(Enable));  // open: Qn, preset, reset
  D_Flip_Flop d_ff_4 (.clk(Clock), .D(Data[3]), .Q(Output[3]), .en(Enable));  // open: Qn, preset, reset
endmodule

// Reg
module _20BitRegister (
  input  Clock,
  input  [19:0] in_2,
  input  Enable,
  output [19:0] out_4
);

  _4BitRegister u_4bitregister_1 (.Clock(Clock), .Data(in_2[3:0]), .Enable(Enable), .Output(out_4[3:0]));
  _4BitRegister u_4bitregister_2 (.Clock(Clock), .Data(in_2[7:4]), .Enable(Enable), .Output(out_4[7:4]));
  _4BitRegister u_4bitregister_3 (.Clock(Clock), .Data(in_2[11:8]), .Enable(Enable), .Output(out_4[11:8]));
  _4BitRegister u_4bitregister_4 (.Clock(Clock), .Data(in_2[15:12]), .Enable(Enable), .Output(out_4[15:12]));
  _4BitRegister u_4bitregister_5 (.Clock(Clock), .Data(in_2[19:16]), .Enable(Enable), .Output(out_4[19:16]));
endmodule

module DLatch (
  input  D,
  input  Clock,
  output Q
);

  wire and_1_out, and_2_out, nor_2_out, not_1_out;

  not not_1 (not_1_out, D);
  and and_1 (and_1_out, not_1_out, Clock);
  and and_2 (and_2_out, Clock, D);
  nor nor_1 (Q, and_1_out, nor_2_out);
  nor nor_2 (nor_2_out, Q, and_2_out);
endmodule

module DFlipFlop (
  input  D,
  input  Clock,
  input  Enable,
  output Q
);

  wire dlatch_1_q, multiplexer_1_out, not_1_out;

  Multiplexer multiplexer_1 (.in0(Q), .in1(D), .out(multiplexer_1_out), .sel(Enable));  // open: en
  not not_1 (not_1_out, Clock);
  DLatch dlatch_1 (.D(multiplexer_1_out), .Clock(not_1_out), .Q(dlatch_1_q));
  DLatch dlatch_2 (.D(dlatch_1_q), .Clock(Clock), .Q(Q));
endmodule

// Reg
module _10BitRegister (
  input  Clock,
  input  [9:0] Data,
  input  Enable,
  output [9:0] Output
);

  D_Flip_Flop d_ff_1 (.clk(Clock), .D(Data[0]), .Q(Output[0]), .en(Enable));  // open: Qn, preset, reset
  D_Flip_Flop d_ff_2 (.clk(Clock), .D(Data[1]), .Q(Output[1]), .en(Enable));  // open: Qn, preset, reset
  D_Flip_Flop d_ff_3 (.clk(Clock), .D(Data[2]), .Q(Output[2]), .en(Enable));  // open: Qn, preset, reset
  D_Flip_Flop d_ff_4 (.clk(Clock), .D(Data[3]), .Q(Output[3]), .en(Enable));  // open: Qn, preset, reset
  D_Flip_Flop d_ff_5 (.clk(Clock), .D(Data[4]), .Q(Output[4]), .en(Enable));  // open: Qn, preset, reset
  D_Flip_Flop d_ff_6 (.clk(Clock), .D(Data[5]), .Q(Output[5]), .en(Enable));  // open: Qn, preset, reset
  D_Flip_Flop d_ff_7 (.clk(Clock), .D(Data[6]), .Q(Output[6]), .en(Enable));  // open: Qn, preset, reset
  D_Flip_Flop d_ff_8 (.clk(Clock), .D(Data[7]), .Q(Output[7]), .en(Enable));  // open: Qn, preset, reset
  D_Flip_Flop d_ff_9 (.clk(Clock), .D(Data[8]), .Q(Output[8]), .en(Enable));  // open: Qn, preset, reset
  D_Flip_Flop d_ff_10 (.clk(Clock), .D(Data[9]), .Q(Output[9]), .en(Enable));  // open: Qn, preset, reset
endmodule

module ControlUnit (
  input  Clock,
  input  [3:0] Opcode,
  output RegWrite,
  output PCWrite,
  output MemWrite,
  output MemRead,
  output Jump,
  output Branch,
  output StackWrite,
  output RegWriteSelect
);

  wire and_1_out, and_2_out, and_3_out, and_4_out, and_10_out, and_11_out, and_12_out, and_13_out,
       and_14_out, and_15_out, and_16_out, and_17_out, and_18_out, and_19_out, and_20_out, and_21_out,
       and_22_out, and_23_out, and_24_out, and_25_out, and_26_out, and_27_out, and_28_out, not_1_out,
       not_2_out, not_3_out, not_4_out, not_5_out, not_6_out, not_7_out, not_8_out, not_9_out, not_10_out,
       not_11_out, not_12_out, not_13_out, not_14_out, not_15_out, not_16_out, not_17_out, not_18_out,
       not_19_out, not_20_out, not_21_out, not_22_out, not_23_out, not_24_out, not_25_out, not_26_out,
       not_27_out, not_28_out, not_29_out, not_30_out, not_31_out, not_32_out, not_33_out, not_34_out,
       not_35_out, not_36_out, not_37_out, not_38_out, not_39_out, not_40_out, not_41_out, not_42_out,
       not_43_out, not_44_out, not_45_out, not_46_out, not_47_out, not_48_out, not_49_out;
  wire [3:0] or_7_out, State_Register_q;

  Register #(.width(4)) State_Register (.D(or_7_out), .Q(State_Register_q), .clk(Clock));  // open: en, clr
  and and_1 (and_1_out, State_Register_q[0], ~State_Register_q[1], ~State_Register_q[2], ~State_Register_q[3]);  // AND_Gate
  or or_1 (RegWrite, and_1_out, and_2_out);
  and and_2 (and_2_out, ~State_Register_q[0], ~State_Register_q[1], ~State_Register_q[2], State_Register_q[3]);  // AND_Gate
  and and_3 (and_3_out, State_Register_q[1], ~State_Register_q[2], ~State_Register_q[3]);  // AND_Gate
  or or_2 (PCWrite, and_3_out, and_4_out);
  and and_4 (and_4_out, ~State_Register_q[0], ~State_Register_q[1], State_Register_q[2], ~State_Register_q[3]);  // AND_Gate
  and and_5 (MemWrite, ~State_Register_q[0], State_Register_q[1], State_Register_q[2], ~State_Register_q[3]);  // AND_Gate
  and and_6 (MemRead, State_Register_q[0], ~State_Register_q[1], State_Register_q[2], ~State_Register_q[3]);  // AND_Gate
  and and_7 (Jump, State_Register_q[0], State_Register_q[1], ~State_Register_q[2], ~State_Register_q[3]);  // AND_Gate
  and and_8 (Branch, ~State_Register_q[0], ~State_Register_q[1], State_Register_q[2], ~State_Register_q[3]);  // AND_Gate
  and and_9 (StackWrite, State_Register_q[0], State_Register_q[1], State_Register_q[2], ~State_Register_q[3]);  // AND_Gate
  or or_3 (RegWriteSelect, MemRead, and_10_out);
  and and_10 (and_10_out, ~State_Register_q[0], ~State_Register_q[1], ~State_Register_q[2], State_Register_q[3]);  // AND_Gate
  not not_1 (not_1_out, State_Register_q[3]);
  not not_2 (not_2_out, State_Register_q[2]);
  not not_3 (not_3_out, State_Register_q[1]);
  not not_4 (not_4_out, State_Register_q[1]);
  not not_5 (not_5_out, Opcode[1]);
  not not_6 (not_6_out, State_Register_q[3]);
  not not_7 (not_7_out, State_Register_q[2]);
  not not_8 (not_8_out, State_Register_q[1]);
  not not_9 (not_9_out, Opcode[1]);
  not not_10 (not_10_out, State_Register_q[1]);
  not not_11 (not_11_out, Opcode[0]);
  not not_12 (not_12_out, State_Register_q[2]);
  not not_13 (not_13_out, State_Register_q[1]);
  not not_14 (not_14_out, State_Register_q[0]);
  not not_15 (not_15_out, Opcode[1]);
  not not_16 (not_16_out, State_Register_q[1]);
  not not_17 (not_17_out, State_Register_q[1]);
  not not_18 (not_18_out, Opcode[1]);
  not not_19 (not_19_out, Opcode[0]);
  not not_20 (not_20_out, State_Register_q[2]);
  not not_21 (not_21_out, State_Register_q[1]);
  not not_22 (not_22_out, Opcode[3]);
  not not_23 (not_23_out, State_Register_q[3]);
  not not_24 (not_24_out, State_Register_q[1]);
  not not_25 (not_25_out, State_Register_q[0]);
  not not_26 (not_26_out, Opcode[3]);
  not not_27 (not_27_out, Opcode[1]);
  not not_28 (not_28_out, State_Register_q[1]);
  not not_29 (not_29_out, State_Register_q[0]);
  not not_30 (not_30_out, Opcode[3]);
  not not_31 (not_31_out, Opcode[2]);
  not not_32 (not_32_out, State_Register_q[1]);
  not not_33 (not_33_out, State_Register_q[0]);
  not not_34 (not_34_out, Opcode[2]);
  not not_35 (not_35_out, Opcode[1]);
  not not_36 (not_36_out, State_Register_q[3]);
  not not_37 (not_37_out, State_Register_q[2]);
  not not_38 (not_38_out, State_Register_q[1]);
  not not_39 (not_39_out, Opcode[3]);
  not not_40 (not_40_out, State_Register_q[1]);
  not not_41 (not_41_out, Opcode[3]);
  not not_42 (not_42_out, State_Register_q[1]);
  not not_43 (not_43_out, Opcode[3]);
  not not_44 (not_44_out, Opcode[2]);
  not not_45 (not_45_out, State_Register_q[0]);
  not not_46 (not_46_out, Opcode[1]);
  not not_47 (not_47_out, State_Register_q[1]);
  not not_48 (not_48_out, Opcode[3]);
  not not_49 (not_49_out, Opcode[2]);
  and and_11 (and_11_out, not_1_out, not_2_out, not_3_out, State_Register_q[0], Opcode[3]);
  and and_12 (and_12_out, State_Register_q[2], not_4_out, not_5_out);
  and and_13 (and_13_out, not_6_out, not_7_out, not_8_out, Opcode[2], not_9_out, Opcode[0]);
  and and_14 (and_14_out, not_10_out, Opcode[2], Opcode[1], not_11_out);
  and and_15 (and_15_out, not_12_out, not_13_out, Opcode[3]);
  and and_16 (and_16_out, State_Register_q[2], not_14_out, not_15_out);
  and and_17 (and_17_out, not_16_out, Opcode[2], Opcode[1]);
  and and_18 (and_18_out, not_17_out, Opcode[3], not_18_out, not_19_out);
  and and_19 (and_19_out, not_20_out, not_21_out, State_Register_q[0], not_22_out);
  and and_20 (and_20_out, State_Register_q[2], State_Register_q[1]);
  and and_21 (and_21_out, not_23_out, not_24_out, not_25_out, not_26_out, not_27_out);
  and and_22 (and_22_out, not_28_out, not_29_out, not_30_out, not_31_out);
  and and_23 (and_23_out, not_32_out, not_33_out, not_34_out, not_35_out, Opcode[0]);
  and and_24 (and_24_out, not_36_out, not_37_out, not_38_out, not_39_out, Opcode[2], Opcode[0]);
  and and_25 (and_25_out, not_40_out, not_41_out, Opcode[2], Opcode[1], Opcode[0]);
  and and_26 (and_26_out, State_Register_q[2], not_42_out, not_43_out, not_44_out);
  and and_27 (and_27_out, State_Register_q[2], not_45_out, not_46_out);
  and and_28 (and_28_out, State_Register_q[3], ~not_47_out, ~not_48_out, ~not_49_out);  // AND_Gate
  or or_4 (or_7_out[3], and_11_out, and_12_out);
  or or_5 (or_7_out[2], and_13_out, and_14_out, and_15_out, and_16_out);
  or or_6 (or_7_out[1], and_17_out, and_18_out, and_19_out, and_20_out, State_Register_q[3]);
  or or_7 (or_7_out[0], and_21_out, and_22_out, and_23_out, and_24_out, and_25_out, and_26_out, and_27_out, and_28_out);
endmodule
