// Logisim project Reptile8.circ as structural Verilog: 9 circuits, main circuit main
module main (
);

  wire alu_1_zeroflag, clock_1_out, controlunit_1_armux, controlunit_1_irload, controlunit_1_memload,
       controlunit_1_mux, controlunit_1_pcinc, controlunit_1_pcload, controlunit_1_regload,
       controlunit_1_zeroflagload, flag_1_out;
  wire [3:0] multiplexer_4_out_2, regbank_1_reg0, regbank_1_reg0_2, regbank_1_reg0_3, regbank_1_reg0_4;
  wire [11:0] adder_1_out, multiplexer_1_out, multiplexer_4_out, n12bitregister_1_dataout,
       programcounter_1_out;
  wire [15:0] alu_1_result, multiplexer_2_out, multiplexer_3_out, ram_1_data, regbank_1_reg1, regbank_1_reg2,
       regbank_1_reg3, regbank_1_reg4, regbank_1_reg5, regbank_1_reg6, regbank_1_reg7;

  Multiplexer #(.width(12)) multiplexer_1 (
    .in0(programcounter_1_out), .in1(multiplexer_4_out), .out(multiplexer_1_out), .sel(controlunit_1_armux));  // open: en
  ProgramCounter programcounter_1 (
    .PcLoad(controlunit_1_pcload), .PcIncrement(controlunit_1_pcinc), .In(adder_1_out),
    .Out(programcounter_1_out), .Clock(clock_1_out));
  Adder #(.width(12)) adder_1 (
    .a(programcounter_1_out), .b(n12bitregister_1_dataout), .out(adder_1_out));  // open: cin, cout
  RAM #(.addrWidth(12), .dataWidth(16), .bus("separate")) ram_1 (
    .addr(multiplexer_1_out), .din(multiplexer_3_out), .data(ram_1_data), .str(controlunit_1_memload),
    .clk(clock_1_out));  // open: sel, ld, clr
  _12BitRegister u_12bitregister_1 (
    .DataIn(ram_1_data[11:0]), .Load(controlunit_1_irload), .Clock(clock_1_out),
    .DataOut(n12bitregister_1_dataout));
  Clock clock_1 (.out(clock_1_out));
  Multiplexer #(.width(16)) multiplexer_2 (
    .in0(alu_1_result), .in1(ram_1_data), .out(multiplexer_2_out), .sel(controlunit_1_mux));  // open: en
  RegBank regbank_1 (
    .WriteAddress(n12bitregister_1_dataout[2:0]), .Clock(clock_1_out), .DataIn(multiplexer_2_out),
    .RegLoad(controlunit_1_regload),
    .Reg0({regbank_1_reg0_4, regbank_1_reg0_3, regbank_1_reg0_2, regbank_1_reg0}), .Reg1(regbank_1_reg1),
    .Reg2(regbank_1_reg2), .Reg3(regbank_1_reg3), .Reg4(regbank_1_reg4), .Reg5(regbank_1_reg5),
    .Reg6(regbank_1_reg6), .Reg7(regbank_1_reg7));
  Multiplexer #(.select(3), .width(16)) multiplexer_3 (
    .in0({regbank_1_reg0_4, regbank_1_reg0_3, regbank_1_reg0_2, regbank_1_reg0}), .in1(regbank_1_reg1),
    .in2(regbank_1_reg2), .in3(regbank_1_reg3), .in4(regbank_1_reg4), .in5(regbank_1_reg5),
    .in6(regbank_1_reg6), .in7(regbank_1_reg7), .out(multiplexer_3_out), .sel(n12bitregister_1_dataout[8:6]));  // open: en
  ALU alu_1 (
    .ir_5_3({multiplexer_4_out_2, multiplexer_4_out}), .ir_8_6(multiplexer_3_out),
    .AluOpcode(n12bitregister_1_dataout[11:6]), .Result(alu_1_result), .ZeroFlag(alu_1_zeroflag));
  Multiplexer #(.select(3), .width(16)) multiplexer_4 (
    .in0({regbank_1_reg0_4, regbank_1_reg0_3, regbank_1_reg0_2, regbank_1_reg0}), .in1(regbank_1_reg1),
    .in2(regbank_1_reg2), .in3(regbank_1_reg3), .in4(regbank_1_reg4), .in5(regbank_1_reg5),
    .in6(regbank_1_reg6), .in7(regbank_1_reg7), .out({multiplexer_4_out_2, multiplexer_4_out}),
    .sel(n12bitregister_1_dataout[5:3]));  // open: en
  Flag flag_1 (.In(alu_1_zeroflag), .FlagLoad(controlunit_1_zeroflagload), .Out(flag_1_out), .Clock(clock_1_out));
  Hex_Digit_Display hex_digit_display_1 (.value(regbank_1_reg0_4));  // open: dp
  ControlUnit controlunit_1 (
    .Opcode(ram_1_data[15:12]), .Zero(flag_1_out), .ARMUX(controlunit_1_armux),
    .IRLOAD(controlunit_1_irload), .Clock(clock_1_out), .REGLOAD(controlunit_1_regload),
    .ZEROFLAGLOAD(controlunit_1_zeroflagload), .MUX(controlunit_1_mux), .MEMLOAD(controlunit_1_memload),
    .PCLOAD(controlunit_1_pcload), .PCINC(controlunit_1_pcinc));
  Hex_Digit_Display hex_digit_display_2 (.value(regbank_1_reg0_3));  // open: dp
  Hex_Digit_Display hex_digit_display_3 (.value(regbank_1_reg0_2));  // open: dp
  Hex_Digit_Display hex_digit_display_4 (.value(regbank_1_reg0));  // open: dp
endmodule

module _4BitRegister (
  input  Load,
  input  Clock,
  input  [3:0] in_3,
  output [3:0] out_4
);

  wire and_1_out, and_2_out, and_3_out, and_4_out, and_5_out, and_6_out, and_7_out, and_8_out;

  and and_1 (and_1_out, in_3[0], Load);
  and and_2 (and_2_out, ~in_3[0], Load);  // AND_Gate
  and and_3 (and_3_out, in_3[1], Load);
  and and_4 (and_4_out, ~in_3[1], Load);  // AND_Gate
  and and_5 (and_5_out, in_3[2], Load);
  and and_6 (and_6_out, ~in_3[2], Load);  // AND_Gate
  and and_7 (and_7_out, in_3[3], Load);
  and and_8 (and_8_out, ~in_3[3], Load);  // AND_Gate
  S_R_Flip_Flop s_r_ff_1 (.S(and_1_out), .clk(Clock), .R(and_2_out), .Q(out_4[0]));  // open: Qn, preset, reset, en
  S_R_Flip_Flop s_r_ff_2 (.S(and_3_out), .clk(Clock), .R(and_4_out), .Q(out_4[1]));  // open: Qn, preset, reset, en
  S_R_Flip_Flop s_r_ff_3 (.S(and_5_out), .clk(Clock), .R(and_6_out), .Q(out_4[2]));  // open: Qn, preset, reset, en
  S_R_Flip_Flop s_r_ff_4 (.S(and_7_out), .clk(Clock), .R(and_8_out), .Q(out_4[3]));  // open: Qn, preset, reset, en
endmodule

module _16BitRegister (
  input  Clock,
  input  Load,
  input  [15:0] in_3,
  output [15:0] out_4
);

  _4BitRegister u_4bitregister_1 (.in_3(in_3[3:0]), .Load(Load), .Clock(Clock), .out_4(out_4[3:0]));
  _4BitRegister u_4bitregister_2 (.in_3(in_3[7:4]), .Load(Load), .Clock(Clock), .out_4(out_4[7:4]));
  _4BitRegister u_4bitregister_3 (.in_3(in_3[11:8]), .Load(Load), .Clock(Clock), .out_4(out_4[11:8]));
  _4BitRegister u_4bitregister_4 (.in_3(in_3[15:12]), .Load(Load), .Clock(Clock), .out_4(out_4[15:12]));
endmodule

// RegisterBank
module RegBank (
  input  RegLoad,
  input  [2:0] WriteAddress,
  input  Clock,
  input  [15:0] DataIn,
  output [15:0] Reg0,
  output [15:0] Reg1,
  output [15:0] Reg2,
  output [15:0] Reg3,
  output [15:0] Reg4,
  output [15:0] Reg5,
  output [15:0] Reg6,
  output [15:0] Reg7
);

  wire and_1_out, and_2_out, and_3_out, and_4_out, and_5_out, and_6_out, and_7_out, and_8_out,
       decoder_1_out0, decoder_1_out1, decoder_1_out2, decoder_1_out3, decoder_1_out4, decoder_1_out5,
       decoder_1_out6, decoder_1_out7;

  Decoder #(.select(3)) decoder_1 (
    .out0(decoder_1_out0), .out1(decoder_1_out1), .out2(decoder_1_out2), .out3(decoder_1_out3),
    .out4(decoder_1_out4), .out5(decoder_1_out5), .out6(decoder_1_out6), .out7(decoder_1_out7),
    .sel(WriteAddress));  // open: en
  and and_1 (and_1_out, decoder_1_out0, RegLoad);
  and and_2 (and_2_out, decoder_1_out1, RegLoad);
  _16BitRegister u_16bitregister_1 (.in_3(DataIn), .Clock(Clock), .Load(and_1_out), .out_4(Reg0));
  _16BitRegister u_16bitregister_2 (.in_3(DataIn), .Clock(Clock), .Load(and_2_out), .out_4(Reg1));
  _16BitRegister u_16bitregister_3 (.in_3(DataIn), .Clock(Clock), .Load(and_3_out), .out_4(Reg2));
  _16BitRegister u_16bitregister_4 (.in_3(DataIn), .Clock(Clock), .Load(and_4_out), .out_4(Reg3));
  _16BitRegister u_16bitregister_5 (.in_3(DataIn), .Clock(Clock), .Load(and_5_out), .out_4(Reg4));
  _16BitRegister u_16bitregister_6 (.in_3(DataIn), .Clock(Clock), .Load(and_6_out), .out_4(Reg5));
  _16BitRegister u_16bitregister_7 (.in_3(DataIn), .Clock(Clock), .Load(and_7_out), .out_4(Reg6));
  _16BitRegister u_16bitregister_8 (.in_3(DataIn), .Clock(Clock), .Load(and_8_out), .out_4(Reg7));
  and and_3 (and_3_out, decoder_1_out2, RegLoad);
  and and_4 (and_4_out, decoder_1_out3, RegLoad);
  and and_5 (and_5_out, decoder_1_out4, RegLoad);
  and and_6 (and_6_out, decoder_1_out5, RegLoad);
  and and_7 (and_7_out, decoder_1_out6, RegLoad);
  and and_8 (and_8_out, decoder_1_out7, RegLoad);
endmodule

// PC
module ProgramCounter (
  input  PcLoad,
  input  Clock,
  input  PcIncrement,
  input  [11:0] In,
  output [11:0] Out
);

  wire or_1_out;
  wire [11:0] adder_1_out, multiplexer_1_out;

  Multiplexer #(.width(12)) multiplexer_1 (
    .in0(In), .in1(adder_1_out), .out(multiplexer_1_out), .sel(PcIncrement));  // open: en
  or or_1 (or_1_out, PcIncrement, PcLoad);
  _12BitRegister u_12bitregister_1 (.DataIn(multiplexer_1_out), .Load(or_1_out), .Clock(Clock), .DataOut(Out));
  Adder #(.width(12)) adder_1 (.a(Out), .b(12'h1), .out(adder_1_out));  // open: cin, cout
endmodule

// IR
module _12BitRegister (
  input  Load,
  input  Clock,
  input  [11:0] DataIn,
  output [11:0] DataOut
);

  _4BitRegister u_4bitregister_1 (.in_3(DataIn[3:0]), .Load(Load), .Clock(Clock), .out_4(DataOut[3:0]));
  _4BitRegister u_4bitregister_2 (.in_3(DataIn[7:4]), .Load(Load), .Clock(Clock), .out_4(DataOut[7:4]));
  _4BitRegister u_4bitregister_3 (.in_3(DataIn[11:8]), .Load(Load), .Clock(Clock), .out_4(DataOut[11:8]));
endmodule

module ALU (
  input  [15:0] ir_5_3,
  input  [15:0] ir_8_6,
  input  [5:0] AluOpcode,
  output [15:0] Result,
  output ZeroFlag
);

  wire and_2_out, or_2_out;
  wire [15:0] adder_1_out, adder_2_out, and_1_out, multiplexer_1_out, multiplexer_2_out, not_1_out, or_1_out,
       subtractor_1_out, subtractor_2_out, xor_1_out;

  Adder #(.width(16)) adder_1 (.a(ir_5_3), .b(ir_8_6), .out(adder_1_out));  // open: cin, cout
  Subtractor #(.width(16)) subtractor_1 (.a(ir_8_6), .b(ir_5_3), .out(subtractor_1_out));  // open: bin, bout
  assign and_1_out = ir_5_3 & ir_8_6;  // AND_Gate and_1, 16 bits wide
  assign or_1_out = ir_5_3 | ir_8_6;  // OR_Gate or_1, 16 bits wide
  assign xor_1_out = ir_5_3 ^ ir_8_6;  // XOR_Gate xor_1, 16 bits wide
  assign not_1_out = ~ir_5_3;  // NOT_Gate not_1, 16 bits wide
  Adder #(.width(16)) adder_2 (.a(ir_5_3), .b(16'h1), .out(adder_2_out));  // open: cin, cout
  Subtractor #(.width(16)) subtractor_2 (.a(ir_5_3), .b(16'h1), .out(subtractor_2_out));  // open: bin, bout
  Multiplexer #(.select(3), .width(16)) multiplexer_1 (
    .in0(not_1_out), .in1(ir_5_3), .in2(adder_2_out), .in3(subtractor_2_out), .out(multiplexer_1_out),
    .sel(AluOpcode[2:0]));  // open: in4, in5, in6, in7, en
  Multiplexer #(.select(3), .width(16)) multiplexer_2 (
    .in0(adder_1_out), .in1(subtractor_1_out), .in2(and_1_out), .in3(or_1_out), .in4(xor_1_out),
    .out(multiplexer_2_out), .sel(AluOpcode[5:3]));  // open: in5, in6, in7, en
  and and_2 (and_2_out, AluOpcode[5], AluOpcode[4], AluOpcode[3]);
  Multiplexer #(.width(16)) multiplexer_3 (
    .in0(multiplexer_2_out), .in1(multiplexer_1_out), .out(Result), .sel(and_2_out));  // open: en
  or or_2 (or_2_out, Result[0], Result[1], Result[2], Result[3], Result[4], Result[5], Result[6], Result[7], Result[8], Result[9], Result[10], Result[11], Result[12], Result[13], Result[14], Result[15]);
  not not_2 (ZeroFlag, or_2_out);
endmodule

// ZF
module Flag (
  input  Clock,
  input  In,
  input  FlagLoad,
  output Out
);

  wire and_1_out, and_2_out;

  and and_1 (and_1_out, In, FlagLoad);
  and and_2 (and_2_out, ~In, FlagLoad);  // AND_Gate
  S_R_Flip_Flop s_r_ff_1 (.S(and_1_out), .clk(Clock), .R(and_2_out), .Q(Out));  // open: Qn, preset, reset, en
endmodule

// Control Unit
module ControlUnit (
  input  [3:0] Opcode,
  input  Zero,
  input  Clock,
  output ARMUX,
  output IRLOAD,
  output REGLOAD,
  output ZEROFLAGLOAD,
  output MUX,
  output MEMLOAD,
  output PCLOAD,
  output PCINC
);

  wire [1:1] and_1_out;
  wire [3:0] multiplexer_1_out, multiplexer_2_out, n4bitregister_1_out_4;
  wire [8:8] rom_1_data;

  and and_1 (and_1_out[1], ~Opcode[3], Opcode[2], ~Opcode[1], ~Opcode[0]);  // AND_Gate
  Multiplexer #(.select(2), .width(4)) multiplexer_1 (
    .in0(Opcode), .in1(Opcode), .in2(4'b0000), .in3(4'b0101), .out(multiplexer_1_out),
    .sel({and_1_out[1], Zero}));  // open: en
  Multiplexer #(.width(4)) multiplexer_2 (
    .in0(4'b0000), .in1(multiplexer_1_out), .out(multiplexer_2_out), .sel(rom_1_data[8]));  // open: en
  _4BitRegister u_4bitregister_1 (.in_3(multiplexer_2_out), .Load(1'b1), .Clock(Clock), .out_4(n4bitregister_1_out_4));
  ROM #(.addrWidth(4), .dataWidth(9)) rom_1 (
    .addr(n4bitregister_1_out_4),
    .data({rom_1_data[8], PCLOAD, PCINC, ARMUX, REGLOAD, ZEROFLAGLOAD, MUX, MEMLOAD, IRLOAD}));  // open: sel

  // Notes on the sheet:
  //   contents of rom_1 (hex, n*v repeats v):
  //   141 54 34 22 0 80 0 18
endmodule
