// Logisim project main.circ as structural Verilog: 14 circuits, main circuit main
module main (
  input  PB2,
  input  [3:0] in_2,
  input  PB1
);

  wire and_1_out, and_2_out, and_3_out, and_4_out, and_5_out, and_6_out, and_7_out, and_8_out, and_9_out,
       and_10_out, and_11_out, clock_1_out, d_ff_1_q, pb2_1_int, pic_1_int, s_r_ff_1_q, timer_1_int,
       vertebratecpu_1_intack, vertebratecpu_1_memld;
  wire [3:0] vertebratecpu_1_dataout;
  wire [11:0] vertebratecpu_1_address;
  wire [15:0] bit_extender_1_out, bit_extender_2_out, multiplexer_1_out, multiplexer_2_out,
       multiplexer_3_out, multiplexer_4_out, multiplexer_5_out, multiplexer_6_out, n16bitregister_1_dataout,
       pb2_1_data, pic_1_vector, ram_1_data, timer_1_timer_value;
  wire [15:4] vertebratecpu_1_dataout_2;

  D_Flip_Flop d_ff_1 (.clk(clock_1_out), .D(PB1), .Q(d_ff_1_q));  // open: Qn, preset, en, reset
  assign bit_extender_1_out = {{12{1'b0}}, in_2};  // Bit_Extender bit_extender_1
  assign bit_extender_2_out = {{15{1'b0}}, s_r_ff_1_q};  // Bit_Extender bit_extender_2
  and and_1 (and_1_out, vertebratecpu_1_address[11], ~vertebratecpu_1_address[10], vertebratecpu_1_address[9], vertebratecpu_1_address[8], ~vertebratecpu_1_address[7], ~vertebratecpu_1_address[6], ~vertebratecpu_1_address[5], ~vertebratecpu_1_address[4], ~vertebratecpu_1_address[3], ~vertebratecpu_1_address[2], ~vertebratecpu_1_address[1], ~vertebratecpu_1_address[0]);  // AND_Gate
  Multiplexer #(.width(16)) multiplexer_1 (
    .in0(bit_extender_1_out), .in1(bit_extender_2_out), .out(multiplexer_1_out),
    .sel(vertebratecpu_1_address[0]));  // open: en
  and and_2 (and_2_out, ~d_ff_1_q, PB1);  // AND_Gate
  and and_3 (and_3_out, ~vertebratecpu_1_address[0], and_9_out);  // AND_Gate
  and and_4 (and_4_out, ~s_r_ff_1_q, and_2_out);  // AND_Gate
  and and_5 (and_5_out, s_r_ff_1_q, and_3_out);
  and and_6 (and_6_out, vertebratecpu_1_address[11], vertebratecpu_1_address[10], ~vertebratecpu_1_address[9], ~vertebratecpu_1_address[8], ~vertebratecpu_1_address[7], ~vertebratecpu_1_address[6], ~vertebratecpu_1_address[5], ~vertebratecpu_1_address[4], ~vertebratecpu_1_address[3], ~vertebratecpu_1_address[2], ~vertebratecpu_1_address[1], ~vertebratecpu_1_address[0]);  // AND_Gate
  S_R_Flip_Flop s_r_ff_1 (
    .S(and_4_out), .clk(clock_1_out), .R(and_5_out), .Q(s_r_ff_1_q));  // open: Qn, preset, reset, en
  _16BitRegister u_16bitregister_1 (
    .DataIn({vertebratecpu_1_dataout_2, vertebratecpu_1_dataout}), .Clock(clock_1_out), .Load(and_7_out),
    .DataOut(n16bitregister_1_dataout));
  and and_7 (and_7_out, and_8_out, vertebratecpu_1_memld);
  and and_8 (and_8_out, vertebratecpu_1_address[11], vertebratecpu_1_address[10], vertebratecpu_1_address[9], ~vertebratecpu_1_address[8], ~vertebratecpu_1_address[7], ~vertebratecpu_1_address[6], ~vertebratecpu_1_address[5], ~vertebratecpu_1_address[4], ~vertebratecpu_1_address[3], ~vertebratecpu_1_address[2], ~vertebratecpu_1_address[1], ~vertebratecpu_1_address[0]);  // AND_Gate
  Hex_Digit_Display hex_digit_display_1 (.value(n16bitregister_1_dataout[15:12]));  // open: dp
  Hex_Digit_Display hex_digit_display_2 (.value(n16bitregister_1_dataout[11:8]));  // open: dp
  Hex_Digit_Display hex_digit_display_3 (.value(n16bitregister_1_dataout[3:0]));  // open: dp
  Hex_Digit_Display hex_digit_display_4 (.value(n16bitregister_1_dataout[7:4]));  // open: dp
  and and_9 (and_9_out, vertebratecpu_1_address[11], vertebratecpu_1_address[10], vertebratecpu_1_address[9], vertebratecpu_1_address[8], ~vertebratecpu_1_address[7], ~vertebratecpu_1_address[6], ~vertebratecpu_1_address[5], ~vertebratecpu_1_address[4], ~vertebratecpu_1_address[3], ~vertebratecpu_1_address[2], ~vertebratecpu_1_address[1]);  // AND_Gate
  and and_10 (and_10_out, vertebratecpu_1_address[11], vertebratecpu_1_address[10], ~vertebratecpu_1_address[9], vertebratecpu_1_address[8], ~vertebratecpu_1_address[7], ~vertebratecpu_1_address[6], ~vertebratecpu_1_address[5], ~vertebratecpu_1_address[4], ~vertebratecpu_1_address[3], ~vertebratecpu_1_address[2], ~vertebratecpu_1_address[1], ~vertebratecpu_1_address[0]);  // AND_Gate
  Multiplexer #(.width(16)) multiplexer_2 (
    .in0(ram_1_data), .in1(pb2_1_data), .out(multiplexer_2_out), .sel(and_1_out));  // open: en
  and and_11 (and_11_out, and_10_out, vertebratecpu_1_memld);
  Multiplexer #(.width(16)) multiplexer_3 (
    .in0(multiplexer_2_out), .in1(timer_1_timer_value), .out(multiplexer_3_out), .sel(and_6_out));  // open: en
  Multiplexer #(.width(16)) multiplexer_4 (
    .in0(multiplexer_3_out), .in1({16{1'b1}}), .out(multiplexer_4_out), .sel(and_8_out));  // open: en
  Multiplexer #(.width(16)) multiplexer_5 (
    .in0(multiplexer_4_out), .in1(multiplexer_1_out), .out(multiplexer_5_out), .sel(and_9_out));  // open: en
  Multiplexer #(.width(16)) multiplexer_6 (
    .in0(multiplexer_5_out), .in1(pic_1_vector), .out(multiplexer_6_out), .sel(vertebratecpu_1_intack));  // open: en
  VertebrateCpu vertebratecpu_1 (
    .DataIn(multiplexer_6_out), .MemLD(vertebratecpu_1_memld), .INT(pic_1_int),
    .INTACK(vertebratecpu_1_intack), .Address(vertebratecpu_1_address),
    .DataOut({vertebratecpu_1_dataout_2, vertebratecpu_1_dataout}), .Clock(clock_1_out));
  Clock clock_1 (.out(clock_1_out));
  PIC pic_1 (
    .Device_0(timer_1_int), .Device_1(pb2_1_int), .Clock(clock_1_out), .MaskLoad(and_11_out),
    .MaskIn(vertebratecpu_1_dataout), .Vector(pic_1_vector), .Int(pic_1_int));  // open: Device_2, Device_3
  RAM #(.addrWidth(12), .dataWidth(16), .bus("separate")) ram_1 (
    .addr(vertebratecpu_1_address), .din({vertebratecpu_1_dataout_2, vertebratecpu_1_dataout}),
    .data(ram_1_data), .str(vertebratecpu_1_memld), .clk(clock_1_out));  // open: sel, ld, clr
  PB2 pb2_1 (.Clock(clock_1_out), .PB2(PB2), .Int(pb2_1_int), .Data(pb2_1_data), .Read(and_1_out));
  Timer timer_1 (.Timer_Value(timer_1_timer_value), .INT(timer_1_int), .Read(and_6_out), .Clock(clock_1_out));
endmodule

module _4BitRegister (
  input  Load,
  input  Clock,
  input  [3:0] DataIn,
  output [3:0] DataOut
);

  wire and_1_out, and_2_out, and_3_out, and_4_out, and_5_out, and_6_out, and_7_out, and_8_out;

  and and_1 (and_1_out, DataIn[0], Load);
  and and_2 (and_2_out, ~DataIn[0], Load);  // AND_Gate
  and and_3 (and_3_out, DataIn[1], Load);
  and and_4 (and_4_out, ~DataIn[1], Load);  // AND_Gate
  and and_5 (and_5_out, DataIn[2], Load);
  and and_6 (and_6_out, ~DataIn[2], Load);  // AND_Gate
  and and_7 (and_7_out, DataIn[3], Load);
  and and_8 (and_8_out, ~DataIn[3], Load);  // AND_Gate
  S_R_Flip_Flop s_r_ff_1 (.S(and_1_out), .clk(Clock), .R(and_2_out), .Q(DataOut[0]));  // open: Qn, preset, reset, en
  S_R_Flip_Flop s_r_ff_2 (.S(and_3_out), .clk(Clock), .R(and_4_out), .Q(DataOut[1]));  // open: Qn, preset, reset, en
  S_R_Flip_Flop s_r_ff_3 (.S(and_5_out), .clk(Clock), .R(and_6_out), .Q(DataOut[2]));  // open: Qn, preset, reset, en
  S_R_Flip_Flop s_r_ff_4 (.S(and_7_out), .clk(Clock), .R(and_8_out), .Q(DataOut[3]));  // open: Qn, preset, reset, en
endmodule

module _16BitRegister (
  input  Clock,
  input  Load,
  input  [15:0] DataIn,
  output [15:0] DataOut
);

  _4BitRegister u_4bitregister_1 (.DataIn(DataIn[3:0]), .Load(Load), .Clock(Clock), .DataOut(DataOut[3:0]));
  _4BitRegister u_4bitregister_2 (.DataIn(DataIn[7:4]), .Load(Load), .Clock(Clock), .DataOut(DataOut[7:4]));
  _4BitRegister u_4bitregister_3 (.DataIn(DataIn[11:8]), .Load(Load), .Clock(Clock), .DataOut(DataOut[11:8]));
  _4BitRegister u_4bitregister_4 (.DataIn(DataIn[15:12]), .Load(Load), .Clock(Clock), .DataOut(DataOut[15:12]));
endmodule

// RegisterBank
module RegBank (
  input  RegLoad,
  input  [2:0] WriteAddress,
  input  Clock,
  input  [15:0] DataIn,
  input  SP_minus_minus,
  input  SP_plus_plus,
  output [15:0] Reg0,
  output [15:0] Reg1,
  output [15:0] Reg2,
  output [15:0] Reg3,
  output [15:0] Reg4,
  output [15:0] Reg5,
  output [15:0] Reg6,
  output [15:0] Reg7
);

  wire and_1_out, and_2_out, and_3_out, and_4_out, and_5_out, and_6_out, and_7_out, and_8_out,
       decoder_1_out0, decoder_1_out1, decoder_1_out2, decoder_1_out3, decoder_1_out4, decoder_1_out5,
       decoder_1_out6, decoder_1_out7, or_1_out, or_2_out;
  wire [15:0] adder_1_out, multiplexer_1_out, multiplexer_2_out;

  Decoder #(.select(3)) decoder_1 (
    .out0(decoder_1_out0), .out1(decoder_1_out1), .out2(decoder_1_out2), .out3(decoder_1_out3),
    .out4(decoder_1_out4), .out5(decoder_1_out5), .out6(decoder_1_out6), .out7(decoder_1_out7),
    .sel(WriteAddress));  // open: en
  or or_1 (or_1_out, SP_minus_minus, SP_plus_plus);
  Multiplexer #(.width(16)) multiplexer_1 (
    .in0(DataIn), .in1(adder_1_out), .out(multiplexer_1_out), .sel(or_1_out));  // open: en
  and and_1 (and_1_out, decoder_1_out1, RegLoad);
  and and_2 (and_2_out, decoder_1_out0, RegLoad);
  _16BitRegister u_16bitregister_1 (.DataIn(DataIn), .Clock(Clock), .Load(and_2_out), .DataOut(Reg0));
  _16BitRegister u_16bitregister_2 (.DataIn(DataIn), .Clock(Clock), .Load(and_1_out), .DataOut(Reg1));
  _16BitRegister u_16bitregister_3 (.DataIn(DataIn), .Clock(Clock), .Load(and_4_out), .DataOut(Reg2));
  _16BitRegister u_16bitregister_4 (.DataIn(DataIn), .Clock(Clock), .Load(and_3_out), .DataOut(Reg3));
  _16BitRegister u_16bitregister_5 (.DataIn(DataIn), .Clock(Clock), .Load(and_6_out), .DataOut(Reg4));
  _16BitRegister u_16bitregister_6 (.DataIn(DataIn), .Clock(Clock), .Load(and_5_out), .DataOut(Reg5));
  _16BitRegister u_16bitregister_7 (.DataIn(DataIn), .Clock(Clock), .Load(and_7_out), .DataOut(Reg6));
  or or_2 (or_2_out, and_8_out, or_1_out);
  _16BitRegister u_16bitregister_8 (.DataIn(multiplexer_1_out), .Clock(Clock), .Load(or_2_out), .DataOut(Reg7));
  Multiplexer #(.width(16)) multiplexer_2 (
    .in0({16{1'b1}}), .in1(16'h1), .out(multiplexer_2_out), .sel(SP_plus_plus));  // open: en
  and and_3 (and_3_out, decoder_1_out3, RegLoad);
  and and_4 (and_4_out, decoder_1_out2, RegLoad);
  Adder #(.width(16)) adder_1 (.a(Reg7), .b(multiplexer_2_out), .out(adder_1_out));  // open: cin, cout
  and and_5 (and_5_out, decoder_1_out5, RegLoad);
  and and_6 (and_6_out, decoder_1_out4, RegLoad);
  and and_7 (and_7_out, decoder_1_out6, RegLoad);
  and and_8 (and_8_out, decoder_1_out7, RegLoad);
endmodule

// PC
module ProgramCounter (
  input  PcLoad,
  input  Clock,
  input  PcIncrement,
  input  [11:0] In,
  output [11:0] Out
);

  wire or_1_out;
  wire [11:0] adder_1_out, multiplexer_1_out;

  Multiplexer #(.width(12)) multiplexer_1 (
    .in0(In), .in1(adder_1_out), .out(multiplexer_1_out), .sel(PcIncrement));  // open: en
  or or_1 (or_1_out, PcIncrement, PcLoad);
  _12BitRegister u_12bitregister_1 (.DataIn(multiplexer_1_out), .Load(or_1_out), .Clock(Clock), .DataOut(Out));
  Adder #(.width(12)) adder_1 (.a(Out), .b(12'h1), .out(adder_1_out));  // open: cin, cout
endmodule

// INTR
module _12BitRegister (
  input  Load,
  input  Clock,
  input  [11:0] DataIn,
  output [11:0] DataOut
);

  _4BitRegister u_4bitregister_1 (.DataIn(DataIn[3:0]), .Load(Load), .Clock(Clock), .DataOut(DataOut[3:0]));
  _4BitRegister u_4bitregister_2 (.DataIn(DataIn[7:4]), .Load(Load), .Clock(Clock), .DataOut(DataOut[7:4]));
  _4BitRegister u_4bitregister_3 (.DataIn(DataIn[11:8]), .Load(Load), .Clock(Clock), .DataOut(DataOut[11:8]));
endmodule

module ALU (
  input  [15:0] ir_5_3,
  input  [15:0] ir_8_6,
  input  [5:0] AluOpcode,
  output [15:0] Result,
  output ZeroFlag
);

  wire and_2_out, or_2_out;
  wire [15:0] adder_1_out, adder_2_out, and_1_out, multiplexer_1_out, multiplexer_2_out, not_1_out, or_1_out,
       shifter_1_out, subtractor_1_out, subtractor_2_out, xor_1_out;

  Adder #(.width(16)) adder_1 (.a(ir_5_3), .b(ir_8_6), .out(adder_1_out));  // open: cin, cout
  Subtractor #(.width(16)) subtractor_1 (.a(ir_8_6), .b(ir_5_3), .out(subtractor_1_out));  // open: bin, bout
  assign and_1_out = ir_5_3 & ir_8_6;  // AND_Gate and_1, 16 bits wide
  assign or_1_out = ir_5_3 | ir_8_6;  // OR_Gate or_1, 16 bits wide
  assign xor_1_out = ir_5_3 ^ ir_8_6;  // XOR_Gate xor_1, 16 bits wide
  assign not_1_out = ~ir_5_3;  // NOT_Gate not_1, 16 bits wide
  Adder #(.width(16)) adder_2 (.a(ir_5_3), .b(16'h1), .out(adder_2_out));  // open: cin, cout
  Subtractor #(.width(16)) subtractor_2 (.a(ir_5_3), .b(16'h1), .out(subtractor_2_out));  // open: bin, bout
  Shifter #(.width(16)) shifter_1 (.in(ir_8_6), .\dist (ir_5_3[3:0]), .out(shifter_1_out));
  Multiplexer #(.select(3), .width(16)) multiplexer_1 (
    .in0(not_1_out), .in1(ir_5_3), .in2(adder_2_out), .in3(subtractor_2_out), .out(multiplexer_1_out),
    .sel(AluOpcode[2:0]));  // open: in4, in5, in6, in7, en
  Multiplexer #(.select(3), .width(16)) multiplexer_2 (
    .in0(adder_1_out), .in1(subtractor_1_out), .in2(and_1_out), .in3(or_1_out), .in4(xor_1_out),
    .in5(shifter_1_out), .out(multiplexer_2_out), .sel(AluOpcode[5:3]));  // open: in6, in7, en
  and and_2 (and_2_out, AluOpcode[5], AluOpcode[4], AluOpcode[3]);
  Multiplexer #(.width(16)) multiplexer_3 (
    .in0(multiplexer_2_out), .in1(multiplexer_1_out), .out(Result), .sel(and_2_out));  // open: en
  not not_2 (ZeroFlag, or_2_out);
  or or_2 (or_2_out, Result[0], Result[1], Result[2], Result[3], Result[4], Result[5], Result[6], Result[7], Result[8], Result[9], Result[10], Result[11], Result[12], Result[13], Result[14], Result[15]);
endmodule

// ZF
module Flag (
  input  D_0,
  input  Clock,
  input  ZFPOP,
  input  ZF,
  input  ZFLD,
  output Out
);

  wire and_1_out, and_2_out, and_3_out, and_4_out, or_1_out, or_2_out;

  and and_1 (and_1_out, D_0, ZFPOP);
  and and_2 (and_2_out, ZF, ZFLD);
  and and_3 (and_3_out, ~D_0, ZFPOP);  // AND_Gate
  and and_4 (and_4_out, ~ZF, ZFLD);  // AND_Gate
  or or_1 (or_1_out, and_1_out, and_2_out);
  or or_2 (or_2_out, and_3_out, and_4_out);
  S_R_Flip_Flop s_r_ff_1 (.S(or_1_out), .clk(Clock), .R(or_2_out), .Q(Out));  // open: Qn, preset, reset, en
endmodule

// Control Unit
module ControlUnit (
  input  [3:0] Opcode,
  input  Zero,
  input  Clock,
  input  INT,
  output [1:0] ARMUX,
  output IRLOAD,
  output REGLOAD,
  output ZEROFLAGLOAD,
  output MUX,
  output MEMLOAD,
  output PCLOAD,
  output PCINC,
  output ZFPOP,
  output [1:0] DATAMUX,
  output SP_plus_plus,
  output SP_minus_minus,
  output PCMUX,
  output INTLD,
  output INTACK
);

  wire and_2_out, and_3_out, s_r_ff_1_q;
  wire [1:1] and_1_out;
  wire [3:0] multiplexer_1_out;
  wire [4:0] bit_extender_1_out, multiplexer_2_out, multiplexer_3_out, n5bitregister_1_dataout, rom_1_data;
  wire [24:22] rom_1_data_2;

  and and_1 (and_1_out[1], ~Opcode[0], ~Opcode[1], Opcode[2], ~Opcode[3]);  // AND_Gate
  Multiplexer #(.select(2), .width(4)) multiplexer_1 (
    .in0(Opcode), .in1(Opcode), .in2(4'b0000), .in3(4'b0101), .out(multiplexer_1_out),
    .sel({and_1_out[1], Zero}));  // open: en
  assign bit_extender_1_out = {{1{1'b0}}, multiplexer_1_out};  // Bit_Extender bit_extender_1
  Multiplexer #(.width(5)) multiplexer_2 (
    .in0(rom_1_data), .in1(bit_extender_1_out), .out(multiplexer_2_out), .sel(rom_1_data_2[24]));  // open: en
  and and_2 (and_2_out, INT, and_3_out, s_r_ff_1_q);
  Multiplexer #(.width(5)) multiplexer_3 (
    .in0(multiplexer_2_out), .in1(5'b10011), .out(multiplexer_3_out), .sel(and_2_out));  // open: en
  _5BitRegister u_5bitregister_1 (
    .DataIn(multiplexer_3_out), .Load(1'b1), .Clock(Clock), .DataOut(n5bitregister_1_dataout));
  and and_3 (and_3_out, ~rom_1_data[4], ~rom_1_data[3], ~rom_1_data[2], ~rom_1_data[1], ~rom_1_data[0]);  // AND_Gate
  ROM #(.addrWidth(5), .dataWidth(25)) rom_1 (
    .addr(n5bitregister_1_dataout),
    .data({rom_1_data_2, INTACK, INTLD, PCMUX, SP_minus_minus, SP_plus_plus, DATAMUX, ZFPOP, PCINC, PCLOAD, MEMLOAD, MUX, ZEROFLAGLOAD, REGLOAD, IRLOAD, ARMUX, rom_1_data}));  // open: sel
  S_R_Flip_Flop s_r_ff_1 (
    .S(rom_1_data_2[22]), .clk(Clock), .R(rom_1_data_2[23]), .Q(s_r_ff_1_q));  // open: Qn, preset, reset, en

  // Notes on the sheet:
  //   contents of rom_1 (hex, n*v repeats v):
  //   1002081 2500 520 820 0 1000 0 300 40840 2000f 49840 20010 400000 800000 20011 540 81040 24452 81040
  //   848854 350855 81060
endmodule

module _5BitRegister (
  input  Load,
  input  Clock,
  input  [4:0] DataIn,
  output [4:0] DataOut
);

  wire and_1_out, and_2_out, and_3_out, and_4_out, and_5_out, and_6_out, and_7_out, and_8_out, and_9_out,
       and_10_out;

  and and_1 (and_1_out, DataIn[0], Load);
  and and_2 (and_2_out, ~DataIn[0], Load);  // AND_Gate
  and and_3 (and_3_out, DataIn[1], Load);
  and and_4 (and_4_out, ~DataIn[1], Load);  // AND_Gate
  and and_5 (and_5_out, DataIn[2], Load);
  and and_6 (and_6_out, ~DataIn[2], Load);  // AND_Gate
  and and_7 (and_7_out, DataIn[3], Load);
  and and_8 (and_8_out, ~DataIn[3], Load);  // AND_Gate
  and and_9 (and_9_out, DataIn[4], Load);
  and and_10 (and_10_out, ~DataIn[4], Load);  // AND_Gate
  S_R_Flip_Flop s_r_ff_1 (.S(and_1_out), .clk(Clock), .R(and_2_out), .Q(DataOut[0]));  // open: Qn, preset, reset, en
  S_R_Flip_Flop s_r_ff_2 (.S(and_3_out), .clk(Clock), .R(and_4_out), .Q(DataOut[1]));  // open: Qn, preset, reset, en
  S_R_Flip_Flop s_r_ff_3 (.S(and_5_out), .clk(Clock), .R(and_6_out), .Q(DataOut[2]));  // open: Qn, preset, reset, en
  S_R_Flip_Flop s_r_ff_4 (.S(and_7_out), .clk(Clock), .R(and_8_out), .Q(DataOut[3]));  // open: Qn, preset, reset, en
  S_R_Flip_Flop s_r_ff_5 (.S(and_9_out), .clk(Clock), .R(and_10_out), .Q(DataOut[4]));  // open: Qn, preset, reset, en
endmodule

// CPU
module VertebrateCpu (
  input  [15:0] DataIn,
  input  Clock,
  input  INT,
  output [11:0] Address,
  output [15:0] DataOut,
  output MemLD,
  output INTACK
);

  wire alu_1_zeroflag, controlunit_1_intld, controlunit_1_irload, controlunit_1_mux, controlunit_1_pcinc,
       controlunit_1_pcload, controlunit_1_pcmux, controlunit_1_regload, controlunit_1_sp_minus_minus,
       controlunit_1_sp_plus_plus, controlunit_1_zeroflagload, controlunit_1_zfpop, flag_1_out;
  wire [1:0] controlunit_1_armux, controlunit_1_datamux;
  wire [3:0] multiplexer_6_out_2;
  wire [11:0] adder_1_out, adder_2_out, bit_extender_1_out, multiplexer_2_out, multiplexer_6_out,
       n12bitregister_1_dataout, n12bitregister_2_dataout, programcounter_1_out, regbank_1_reg7;
  wire [15:0] alu_1_result, bit_extender_2_out, bit_extender_3_out, multiplexer_4_out, multiplexer_5_out,
       regbank_1_reg0, regbank_1_reg1, regbank_1_reg2, regbank_1_reg3, regbank_1_reg4, regbank_1_reg5,
       regbank_1_reg6;
  wire [15:12] regbank_1_reg7_2;

  _12BitRegister u_12bitregister_1 (
    .DataIn(adder_1_out), .Load(controlunit_1_intld), .Clock(Clock), .DataOut(n12bitregister_1_dataout));
  Adder #(.width(12)) adder_1 (.a(12'h7f0), .b(bit_extender_1_out), .out(adder_1_out));  // open: cin, cout
  assign bit_extender_1_out = {{9{1'b0}}, DataIn[2:0]};  // Bit_Extender bit_extender_1
  Multiplexer #(.select(2), .width(12)) multiplexer_1 (
    .in0(programcounter_1_out), .in1(multiplexer_6_out), .in2(regbank_1_reg7),
    .in3(n12bitregister_1_dataout), .out(Address), .sel(controlunit_1_armux));  // open: en
  ProgramCounter programcounter_1 (
    .PcLoad(controlunit_1_pcload), .PcIncrement(controlunit_1_pcinc), .In(multiplexer_2_out),
    .Out(programcounter_1_out), .Clock(Clock));
  Multiplexer #(.width(12)) multiplexer_2 (
    .in0(adder_2_out), .in1(DataIn[11:0]), .out(multiplexer_2_out), .sel(controlunit_1_pcmux));  // open: en
  Adder #(.width(12)) adder_2 (
    .a(programcounter_1_out), .b(n12bitregister_2_dataout), .out(adder_2_out));  // open: cin, cout
  assign bit_extender_2_out = {{4{1'b0}}, programcounter_1_out};  // Bit_Extender bit_extender_2
  Multiplexer #(.select(2), .width(16)) multiplexer_3 (
    .in0(multiplexer_5_out), .in1(bit_extender_2_out), .in2(bit_extender_3_out), .out(DataOut),
    .sel(controlunit_1_datamux));  // open: in3, en
  assign bit_extender_3_out = {{15{1'b0}}, flag_1_out};  // Bit_Extender bit_extender_3
  _12BitRegister u_12bitregister_2 (
    .DataIn(DataIn[11:0]), .Load(controlunit_1_irload), .Clock(Clock), .DataOut(n12bitregister_2_dataout));
  Multiplexer #(.width(16)) multiplexer_4 (
    .in0(alu_1_result), .in1(DataIn), .out(multiplexer_4_out), .sel(controlunit_1_mux));  // open: en
  RegBank regbank_1 (
    .WriteAddress(n12bitregister_2_dataout[2:0]), .Clock(Clock), .DataIn(multiplexer_4_out),
    .SP_minus_minus(controlunit_1_sp_minus_minus), .SP_plus_plus(controlunit_1_sp_plus_plus),
    .RegLoad(controlunit_1_regload), .Reg0(regbank_1_reg0), .Reg1(regbank_1_reg1), .Reg2(regbank_1_reg2),
    .Reg3(regbank_1_reg3), .Reg4(regbank_1_reg4), .Reg5(regbank_1_reg5), .Reg6(regbank_1_reg6),
    .Reg7({regbank_1_reg7_2, regbank_1_reg7}));
  Multiplexer #(.select(3), .width(16)) multiplexer_5 (
    .in0(regbank_1_reg0), .in1(regbank_1_reg1), .in2(regbank_1_reg2), .in3(regbank_1_reg3),
    .in4(regbank_1_reg4), .in5(regbank_1_reg5), .in6(regbank_1_reg6),
    .in7({regbank_1_reg7_2, regbank_1_reg7}), .out(multiplexer_5_out), .sel(n12bitregister_2_dataout[8:6]));  // open: en
  ALU alu_1 (
    .ir_5_3({multiplexer_6_out_2, multiplexer_6_out}), .ir_8_6(multiplexer_5_out),
    .AluOpcode(n12bitregister_2_dataout[11:6]), .Result(alu_1_result), .ZeroFlag(alu_1_zeroflag));
  Multiplexer #(.select(3), .width(16)) multiplexer_6 (
    .in0(regbank_1_reg0), .in1(regbank_1_reg1), .in2(regbank_1_reg2), .in3(regbank_1_reg3),
    .in4(regbank_1_reg4), .in5(regbank_1_reg5), .in6(regbank_1_reg6),
    .in7({regbank_1_reg7_2, regbank_1_reg7}), .out({multiplexer_6_out_2, multiplexer_6_out}),
    .sel(n12bitregister_2_dataout[5:3]));  // open: en
  Flag flag_1 (
    .ZF(alu_1_zeroflag), .Out(flag_1_out), .Clock(Clock), .ZFLD(controlunit_1_zeroflagload), .D_0(DataIn[0]),
    .ZFPOP(controlunit_1_zfpop));
  ControlUnit controlunit_1 (
    .Opcode(DataIn[15:12]), .Zero(flag_1_out), .ARMUX(controlunit_1_armux), .IRLOAD(controlunit_1_irload),
    .Clock(Clock), .REGLOAD(controlunit_1_regload), .ZEROFLAGLOAD(controlunit_1_zeroflagload),
    .MUX(controlunit_1_mux), .MEMLOAD(MemLD), .PCLOAD(controlunit_1_pcload), .PCINC(controlunit_1_pcinc),
    .DATAMUX(controlunit_1_datamux), .SP_plus_plus(controlunit_1_sp_plus_plus),
    .SP_minus_minus(controlunit_1_sp_minus_minus), .PCMUX(controlunit_1_pcmux), .ZFPOP(controlunit_1_zfpop),
    .INTLD(controlunit_1_intld), .INT(INT), .INTACK(INTACK));
endmodule

module PIC (
  input  Device_0,
  input  Device_1,
  input  Device_2,
  input  Device_3,
  input  Clock,
  input  MaskLoad,
  input  [3:0] MaskIn,
  output [15:0] Vector,
  output Int
);

  wire and_1_out, and_2_out, and_3_out, and_4_out;
  wire [1:0] priority_encoder_1_out;
  wire [3:0] n4bitregister_1_dataout;

  _4BitRegister u_4bitregister_1 (.DataIn(MaskIn), .Load(MaskLoad), .Clock(Clock), .DataOut(n4bitregister_1_dataout));
  and and_1 (and_1_out, Device_0, ~n4bitregister_1_dataout[0]);  // AND_Gate
  and and_2 (and_2_out, Device_1, ~n4bitregister_1_dataout[1]);  // AND_Gate
  and and_3 (and_3_out, Device_2, ~n4bitregister_1_dataout[2]);  // AND_Gate
  and and_4 (and_4_out, Device_3, ~n4bitregister_1_dataout[3]);  // AND_Gate
  Priority_Encoder #(.select(2)) priority_encoder_1 (
    .in0(and_1_out), .in1(and_2_out), .in2(and_3_out), .in3(and_4_out), .out(priority_encoder_1_out), .gs(Int));  // open: en_out, en_in
  assign Vector = {{14{1'b0}}, priority_encoder_1_out};  // Bit_Extender bit_extender_1
endmodule

module Timer (
  input  Clock,
  input  Read,
  output [15:0] Timer_Value,
  output INT
);

  wire and_1_out, and_2_out, and_3_out, d_ff_1_q;
  wire [15:0] adder_1_out, adder_2_out, n16bitregister_1_dataout;

  Adder #(.width(16)) adder_1 (.a(n16bitregister_1_dataout), .b(16'h1), .out(adder_1_out));  // open: cin, cout
  _16BitRegister u_16bitregister_1 (
    .DataIn(adder_1_out), .Clock(Clock), .Load(1'b1), .DataOut(n16bitregister_1_dataout));
  Adder #(.width(16)) adder_2 (.a(Timer_Value), .b(16'h1), .out(adder_2_out));  // open: cin, cout
  _16BitRegister u_16bitregister_2 (
    .DataIn(adder_2_out), .Clock(n16bitregister_1_dataout[9]), .Load(1'b1), .DataOut(Timer_Value));
  D_Flip_Flop d_ff_1 (.clk(Clock), .D(n16bitregister_1_dataout[9]), .Q(d_ff_1_q));  // open: Qn, preset, en, reset
  and and_1 (and_1_out, ~d_ff_1_q, n16bitregister_1_dataout[9]);  // AND_Gate
  and and_2 (and_2_out, ~INT, and_1_out);  // AND_Gate
  and and_3 (and_3_out, INT, Read);
  S_R_Flip_Flop s_r_ff_1 (.S(and_2_out), .clk(Clock), .R(and_3_out), .Q(INT));  // open: Qn, preset, reset, en
endmodule

module PB2 (
  input  Clock,
  input  PB2,
  input  Read,
  output Int,
  output [15:0] Data
);

  wire and_1_out, and_2_out, and_3_out, d_ff_1_q, d_ff_2_q, d_ff_3_q, xor_1_out;

  D_Flip_Flop d_ff_1 (.clk(Clock), .D(PB2), .Q(d_ff_1_q));  // open: Qn, preset, en, reset
  D_Flip_Flop d_ff_2 (.clk(Clock), .D(d_ff_1_q), .Q(d_ff_2_q));  // open: Qn, preset, en, reset
  xor xor_1 (xor_1_out, d_ff_2_q, d_ff_1_q);
  D_Flip_Flop d_ff_3 (.clk(Clock), .D(xor_1_out), .Q(d_ff_3_q));  // open: Qn, preset, en, reset
  and and_1 (and_1_out, ~d_ff_3_q, xor_1_out);  // AND_Gate
  and and_2 (and_2_out, ~Int, and_1_out);  // AND_Gate
  S_R_Flip_Flop s_r_ff_1 (.S(and_2_out), .clk(Clock), .R(and_3_out), .Q(Int));  // open: Qn, preset, reset, en
  and and_3 (and_3_out, Int, Read);
  assign Data = {{15{1'b0}}, PB2};  // Bit_Extender bit_extender_1
endmodule
